# Fritzing sketch fritzing-view (saved by Fritzing 0.9.2b)
circuit board: 8.46667cm x 5.64444cm

parts:
  J1 = Piezo Speaker
  V1 = DC Power [voltage=5]
  S3 = Pushbutton [package="[THT]"]
  S4 = Pushbutton [package="[THT]"]
  S5 = Pushbutton [package="[THT]"]
  S6 = Pushbutton [package="[THT]"]
  S7 = Pushbutton [package="[THT]"]
  Part1 = Arduino Pro Mini v13
  VCC1 = Battery
  Part2 = 24 NeoPixel Ring [part_number=1586]

nets:
  GND: J1.pin1, V1.V-, S3.Pin_3, S3.Pin_4, S4.Pin_3, S5.Pin_3, S6.Pin_3, S6.Pin_4, S7.Pin_3, S7.Pin_4, Part1.GND, VCC1.-, Part2.GND
  N1: J1.pin2, Part1.D8
  VCC: V1.V+, Part1.VCC, VCC1.+, Part2.VDD
  N2: S3.Pin_2, Part1.A1
  N3: S4.Pin_2, Part1.A0
  N4: S5.Pin_2, Part1.D12/MISO
  N5: Part1.D10_PWM/SS, Part2.IN

custom parts:
  24 NeoPixel Ring: 24 ultra bright smart LED NeoPixels are arranged in a circle with 2.6" (66mm) outer diameter. The rings are 'chainable' - connect the output pin of one to the input pin of another. Use only one microcontroller pin to control as many as you can chain together! Each LED is addressable as the driver chip is inside the LED. Each one has ~18mA constant current drive so the color will be very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
